# Fritzing sketch drumduino (saved by Fritzing 0.9.2b)
breadboards: 1

parts:
  Arduino = Arduino Uno (Rev3)
  R1 = Resistor [tolerance=±5% resistance=1M package=THT]
  TX_SWITCH = male pin header, 3 pins [form="♂ (male)"]
  RX_SWITCH = male alternating pin header, 3 pins [form="♂ (male)"]
  MIDI_IN = DIN-5 jack (MIDI) [package=THT]
  MIDI_THRU = DIN-5 jack (MIDI) [package=THT]
  MIDI_OUT = DIN-5 jack (MIDI) [package=THT]
  R2 = Resistor [tolerance=±5% resistance=1M package=THT]
  R4 = Resistor [tolerance=±5% resistance=1M package=THT]
  R5 = Resistor [tolerance=±5% resistance=1M package=THT]
  R6 = Resistor [tolerance=±5% resistance=1M package=THT]
  LCD1 = LCD screen [part_number=hd44780]
  R7 = Trimmer Potentiometer [maximum_resistance=10kΩ package=THT]
  IC7 = 6N139 [chip_label=6N139 package="DIP (Dual Inline) [THT]"]
  R8 = Resistor [tolerance=±5% resistance=220 package=THT]
  R9 = Resistor [tolerance=±5% resistance=3.3k package=THT]
  D1 = 1N4148 [part_number=1N4148 package="300 mil [THT]"]
  IC8 = 74HC4851N [chip_label="74HC4851N " package="DIP (Dual Inline) [THT]"]
  IC9 = 74HC4851N [chip_label="74HC4851N " package="DIP (Dual Inline) [THT]"]
  IC10 = 74HC4851N [chip_label="74HC4851N " package="DIP (Dual Inline) [THT]"]
  IC11 = 74HC4851N [chip_label="74HC4851N " package="DIP (Dual Inline) [THT]"]
  IC12 = 74HC4851N [chip_label="74HC4851N " package="DIP (Dual Inline) [THT]"]
  IC13 = 74HC4851N [chip_label="74HC4851N " package="DIP (Dual Inline) [THT]"]
  R3 = Resistor [tolerance=±5% resistance=1M package=THT]

nets:
  AD_0: Arduino.A0, R1.Pin_0, IC8.COM
  AD_1: Arduino.A1, R2.Pin_0, IC9.COM
  AD_2: Arduino.A2, IC10.COM, R3.Pin_0
  AD_3: Arduino.A3, R4.Pin_0, IC11.COM
  AD_4: Arduino.A4/SDA, R5.Pin_0, IC12.COM
  AD_5: Arduino.A5/SCL, R6.Pin_0, IC13.COM
  GND: Arduino.GND, R1.Pin_1, MIDI_IN.GND, MIDI_THRU.GND, MIDI_OUT.GND, R2.Pin_1, R4.Pin_1, R5.Pin_1, R6.Pin_1, LCD1.VSS, LCD1.R/W, LCD1.LED-, R7.leg1, IC7.GND, IC8.INH, IC8.GND, IC9.INH, IC9.GND, IC10.INH, IC10.GND, IC11.INH, IC11.GND, IC12.INH, IC12.GND, IC13.INH, IC13.GND, R3.Pin_1
  ARDUINO_RX: Arduino.D0/RX, RX_SWITCH.pin1
  ARDUINO_TX: Arduino.D1/TX, TX_SWITCH.pin1
  SOFTSERIAL_RX: Arduino.D2, RX_SWITCH.pin3
  SOFTSERIAL_TX: Arduino.D3_PWM, TX_SWITCH.pin3
  DMUX_A: Arduino.D4, IC8.A, IC9.A, IC10.A, IC11.A, IC12.A, IC13.A
  DMUX_B: Arduino.D5_PWM, IC8.B, IC9.B, IC10.B, IC11.B, IC12.B, IC13.B
  DMUX_C: Arduino.D6_PWM, IC8.C, IC9.C, IC10.C, IC11.C, IC12.C, IC13.C
  3.3V: Arduino.3V3
  5V: Arduino.5V, LCD1.VDD, LCD1.LED+, R7.wiper, IC7.VCC, R9.Pin_0, IC8.VCC, IC9.VCC, IC10.VCC, IC11.VCC, IC12.VCC, IC13.VCC
  TX: TX_SWITCH.pin2
  RX: RX_SWITCH.pin2, IC7.VO, R9.Pin_1
  N1: MIDI_IN.5, IC7.Vf-, D1.anode
  N2: MIDI_IN.4, R8.Pin_0
  LCD_INTENSITY: LCD1.V0, R7.leg2
  LCD_RS: LCD1.RS
  LCD_E: LCD1.E
  LCD_DB4: LCD1.DB4
  LCD_DB5: LCD1.DB5
  LCD_DB6: LCD1.DB6
  LCD_DB7: LCD1.DB7
  N3: IC7.Vf+, R8.Pin_1, D1.cathode
  PORT_A_4: IC8.Y4
  PORT_A_6: IC8.Y6
  PORT_A_7: IC8.Y7
  PORT_A_5: IC8.Y5
  PORT_A_3: IC8.Y3
  PORT_A_0: IC8.Y0
  PORT_A_1: IC8.Y1
  PORT_A_2: IC8.Y2
  PORT_B_4: IC9.Y4
  PORT_B_6: IC9.Y6
  PORT_B_7: IC9.Y7
  PORT_B_5: IC9.Y5
  PORT_B_3: IC9.Y3
  PORT_B_0: IC9.Y0
  PORT_B_1: IC9.Y1
  PORT_B_2: IC9.Y2
  PORT_C_4: IC10.Y4
  PORT_C_6: IC10.Y6
  PORT_C_7: IC10.Y7
  PORT_C_5: IC10.Y5
  PORT_C_3: IC10.Y3
  PORT_C_0: IC10.Y0
  PORT_C_1: IC10.Y1
  PORT_C_2: IC10.Y2
  PORT_D_4: IC11.Y4
  PORT_D_6: IC11.Y6
  PORT_D_7: IC11.Y7
  PORT_D_5: IC11.Y5
  PORT_D_3: IC11.Y3
  PORT_D_0: IC11.Y0
  PORT_D_1: IC11.Y1
  PORT_D_2: IC11.Y2
  PORT_E_4: IC12.Y4
  PORT_E_6: IC12.Y6
  PORT_E_7: IC12.Y7
  PORT_E_5: IC12.Y5
  PORT_E_3: IC12.Y3
  PORT_E_0: IC12.Y0
  PORT_E_1: IC12.Y1
  PORT_E_2: IC12.Y2
  PORT_F_4: IC13.Y4
  PORT_F_6: IC13.Y6
  PORT_F_7: IC13.Y7
  PORT_F_5: IC13.Y5
  PORT_F_3: IC13.Y3
  PORT_F_0: IC13.Y0
  PORT_F_1: IC13.Y1
  PORT_F_2: IC13.Y2

custom parts:
  6N139: DARLINGTON OPTOCOUPLERS The 6N138/9 and HCPL-2730/HCPL-2731 optocouplers consist of an AlGaAs LED optically coupled to a high gain split darlington photodetector. The split darlington configuration separating the input photodiode and the first stage gain from the output transistor permits lower output saturation voltage and higher speed operation than possible with conventional darlington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
  1N4148: Small Signal Fast Switching Diode
  74HC4851N: 8-Channel Analog Multiplexer/Demultiplexer with Injection-Current Effect Control
